// Logisim project Data Memory.circ as structural Verilog: 1 circuit, main circuit main
module main (
  input  [7:0] Address,
  input  [3:0] Data,
  input  MemWrite,
  input  MemRead,
  output [3:0] out
);

  wire Clk_out;

  Clock Clk (.out(Clk_out));
  RAM #(.dataWidth(4), .bus("separate")) ram_1 (
    .addr(Address), .din(Data), .data(out), .str(MemWrite), .sel(1'b1), .clk(Clk_out), .ld(MemRead),
    .clr(1'b0));
endmodule
