// Logisim project Instruction Memory.circ as structural Verilog: 1 circuit, main circuit main
module main (
  input  [7:0] in_1,
  output [15:0] out_2
);

  ROM #(.dataWidth(16)) rom_1 (.addr(in_1), .data(out_2), .sel(1'b1));

  // Notes on the sheet:
  //   contents of rom_1 (hex, n*v repeats v):
  //   aafa 2123 14*0 dfa1 7*0 ad
endmodule
